// Logisim project FWGC.circ as structural Verilog: 5 circuits, main circuit ALARM
module main (
  input  in_1,
  input  in_2,
  input  in_3,
  input  in_4,
  input  in_5
);

  wire button_1_out, button_2_out, button_3_out, button_4_out, button_5_out, clock_1_out, move_state_1_out_5,
       move_state_1_out_6, move_state_1_out_7, move_state_1_out_8, n7_segment_1_da, n7_segment_1_db,
       n7_segment_1_dc, n7_segment_1_dd, n7_segment_1_de, n7_segment_1_df, n7_segment_1_dg, switch_1_out_2,
       switch_1_out_3, switch_2_out_2, switch_2_out_3, switch_3_out_2, switch_3_out_3, switch_4_out_2,
       switch_4_out_3;
  wire [6:0] rom_1_data;
  wire [7:0] counter_1_q;

  Counter #(.ongoal("stay")) counter_1 (
    .load(in_5), .Q(counter_1_q), .clk(clock_1_out), .clr(button_1_out));  // open: D, count, carry
  Button button_1 (.out(button_1_out));
  Clock #(.highDuration(3), .lowDuration(3)) clock_1 (.out(clock_1_out));
  ROM #(.dataWidth(7)) rom_1 (.addr(counter_1_q), .data(rom_1_data));  // open: sel
  _7_Segment u_7_segment_1 (
    .in_1(in_1), .in_2(in_2), .in_3(in_3), .in_4(in_4), .DA(n7_segment_1_da), .DB(n7_segment_1_db),
    .DC(n7_segment_1_dc), .DD(n7_segment_1_dd), .DE(n7_segment_1_de), .DF(n7_segment_1_df),
    .DG(n7_segment_1_dg));
  _7_Segment_Display u_7_segment_display_1 (
    .g(n7_segment_1_dg), .f(n7_segment_1_df), .a(n7_segment_1_da), .b(n7_segment_1_db), .e(n7_segment_1_de),
    .d(n7_segment_1_dd), .c(n7_segment_1_dc));  // open: dp
  TTY tty_1 (.data(rom_1_data), .clk(clock_1_out), .clr(button_1_out));  // open: we
  LED led_1 (.in(switch_4_out_2));
  LED led_2 (.in(switch_3_out_2));
  LED led_3 (.in(switch_2_out_2));
  LED led_4 (.in(switch_1_out_2));
  LED led_5 (.in(switch_4_out_3));
  LED led_6 (.in(switch_3_out_3));
  LED led_7 (.in(switch_2_out_3));
  LED led_8 (.in(switch_1_out_3));
  switch switch_1 (.in_1(move_state_1_out_8), .out_2(switch_1_out_2), .out_3(switch_1_out_3));
  switch switch_2 (.in_1(move_state_1_out_7), .out_2(switch_2_out_2), .out_3(switch_2_out_3));
  switch switch_3 (.in_1(move_state_1_out_6), .out_2(switch_3_out_2), .out_3(switch_3_out_3));
  switch switch_4 (.in_1(move_state_1_out_5), .out_2(switch_4_out_2), .out_3(switch_4_out_3));
  Move_State move_state_1 (
    .in_1(button_2_out), .in_2(button_3_out), .in_3(button_4_out), .in_4(button_5_out),
    .out_5(move_state_1_out_5), .out_6(move_state_1_out_6), .out_7(move_state_1_out_7),
    .out_8(move_state_1_out_8));
  Button button_2 (.out(button_2_out));
  Button button_3 (.out(button_3_out));
  Button button_4 (.out(button_4_out));
  Button button_5 (.out(button_5_out));

  // Notes on the sheet:
  //   contents of rom_1 (hex, n*v repeats v):
  //   57 65 6c 63 6f 6d 65 21 20 54 6f 20 74 68 65 20 46 61 72 6d 65 72 2c 20 57 6f 6c 66 2c 20 47 6f 61
  //   74 2c 20 61 6e 64 20 43 61 62 62 61 67 65 20 67 61 6d 65 2e 20 49 6e 73 74 72 75 63 74 69 6f 6e 73
  //   3a 20 41 20 66 61 72 6d 65 72 2c 20 61 20 67 6f 61 74 2c 20 61 20 77 6f 6c 66 2c 20 61 6e 64 20 61
  //   20 63 61 62 62 61 67 65 20 68 61 76 65 20 74 6f 20 63 72 6f 73 73 20 61 20 72 69 76 65 72 2e 20 41
  //   20 62 6f 61 74 20
  //   Moves
  //   West
  //   East
  //   Go alone
  //   Take Wolf
  //   Take Goat
  //   Take Cabbage
endmodule

module ALARM (
  input  in_1,
  input  in_2,
  input  in_3,
  input  in_4,
  output out_5,
  output out_6,
  output out_7,
  output out_8
);

  wire and_1_out, and_2_out, and_3_out, and_4_out, not_1_out, not_2_out, not_3_out, not_4_out, not_5_out,
       not_6_out, or_1_out;

  not not_1 (not_1_out, in_1);
  not not_2 (not_2_out, in_3);
  not not_3 (not_3_out, in_1);
  not not_4 (not_4_out, in_2);
  not not_5 (not_5_out, in_4);
  not not_6 (not_6_out, in_3);
  and and_1 (and_1_out, not_1_out, not_2_out);
  and and_2 (and_2_out, in_1, in_3);
  and and_3 (and_3_out, not_3_out, not_4_out, not_5_out);
  and and_4 (and_4_out, in_2, not_6_out, in_4);
  or or_1 (or_1_out, and_1_out, and_2_out, and_3_out, and_4_out);
  and and_5 (out_5, or_1_out, in_1);
  and and_6 (out_6, or_1_out, in_2);
  and and_7 (out_7, or_1_out, in_3);
  and and_8 (out_8, or_1_out, in_4);

  // Notes on the sheet:
  //   Farmer
  //   Wolf
  //   Goat
  //   Cabbage
  //   This is the logic for the alarm.
  //   Need a West alarm and a East alarm
endmodule

module _7_Segment (
  input  in_1,
  input  in_2,
  input  in_3,
  input  in_4,
  output DA,
  output DB,
  output DC,
  output DD,
  output DE,
  output DF,
  output DG
);

  wire and_1_out, and_2_out, and_3_out, and_4_out, and_5_out, and_6_out, and_7_out, and_8_out, and_9_out,
       and_10_out, and_11_out, and_12_out, and_13_out, and_14_out, and_15_out, and_16_out, and_17_out,
       and_18_out, and_19_out, and_20_out, and_21_out, and_22_out, and_23_out, and_24_out, and_25_out,
       and_26_out, and_27_out, and_28_out;

  and and_1 (and_1_out, ~in_1, in_3);  // AND_Gate
  and and_2 (and_2_out, ~in_1, in_2, in_4);  // AND_Gate
  and and_3 (and_3_out, ~in_2, ~in_3, ~in_4);  // AND_Gate
  and and_4 (and_4_out, in_1, ~in_2, ~in_3);  // AND_Gate
  and and_5 (and_5_out, ~in_1, ~in_3, ~in_4);  // AND_Gate
  and and_6 (and_6_out, ~in_2, ~in_3, ~in_4);  // AND_Gate
  and and_7 (and_7_out, ~in_1, in_3, in_4);  // AND_Gate
  and and_8 (and_8_out, ~in_1, ~in_2, in_3);  // AND_Gate
  and and_9 (and_9_out, in_1, ~in_2, ~in_3);  // AND_Gate
  and and_10 (and_10_out, ~in_1, in_2);  // AND_Gate
  and and_11 (and_11_out, ~in_1, ~in_3, ~in_4);  // AND_Gate
  and and_12 (and_12_out, ~in_1, in_3, in_4);  // AND_Gate
  and and_13 (and_13_out, in_1, ~in_2, ~in_3);  // AND_Gate
  and and_14 (and_14_out, ~in_1, in_2, ~in_3, in_4);  // AND_Gate
  and and_15 (and_15_out, ~in_2, ~in_3, ~in_4);  // AND_Gate
  and and_16 (and_16_out, ~in_1, ~in_2, in_3);  // AND_Gate
  and and_17 (and_17_out, ~in_1, in_3, ~in_4);  // AND_Gate
  and and_18 (and_18_out, ~in_2, ~in_3, ~in_4);  // AND_Gate
  and and_19 (and_19_out, ~in_1, ~in_2, ~in_3);  // AND_Gate
  and and_20 (and_20_out, ~in_1, in_3, ~in_4);  // AND_Gate
  and and_21 (and_21_out, ~in_1, ~in_3);  // AND_Gate
  and and_22 (and_22_out, in_1, ~in_2, ~in_3);  // AND_Gate
  and and_23 (and_23_out, ~in_1, in_2, ~in_4, in_3);  // AND_Gate
  and and_24 (and_24_out, in_1, ~in_2, ~in_3);  // AND_Gate
  and and_25 (and_25_out, ~in_1, in_2, ~in_3);  // AND_Gate
  and and_26 (and_26_out, ~in_1, ~in_2, in_3);  // AND_Gate
  and and_27 (and_27_out, ~in_1, in_3, ~in_4);  // AND_Gate
  and and_28 (and_28_out, ~in_1, ~in_3, ~in_4);  // AND_Gate
  or or_1 (DA, and_1_out, and_2_out, and_3_out, and_4_out);
  or or_2 (DB, and_5_out, and_6_out, and_7_out, and_8_out, and_9_out);
  or or_3 (DC, and_10_out, and_11_out, and_12_out, and_13_out);
  or or_4 (DD, and_14_out, and_15_out, and_16_out, and_17_out);
  or or_5 (DE, and_18_out, and_19_out, and_20_out);
  or or_6 (DF, and_21_out, and_22_out, and_23_out);
  or or_7 (DG, and_24_out, and_25_out, and_26_out, and_27_out);
endmodule

module Move_State (
  input  in_1,
  input  in_2,
  input  in_3,
  input  in_4,
  output out_5,
  output out_6,
  output out_7,
  output out_8
);

  wire or_1_out;

  or or_1 (or_1_out, in_1, in_2, in_3, in_4);
  ALARM alarm_1 (
    .in_1(or_1_out), .in_2(in_2), .in_3(in_3), .in_4(in_4), .out_5(out_5), .out_6(out_6), .out_7(out_7),
    .out_8(out_8));

  // Notes on the sheet:
  //   Farmer
  //   Wolf
  //   Goat
  //   Cabbage
  //   This is the logic for the alarm.
  //   Need a West alarm and a East alarm
endmodule

module switch (
  input  in_1,
  output out_2,
  output out_3
);

  wire d_ff_1_qn, d_ff_2_q, d_ff_2_qn;

  D_Flip_Flop d_ff_1 (.clk(in_1), .D(d_ff_2_qn), .Qn(d_ff_1_qn));  // open: Q, preset, en, reset
  D_Flip_Flop d_ff_2 (.clk(in_1), .D(d_ff_1_qn), .Q(d_ff_2_q), .Qn(d_ff_2_qn));  // open: preset, en, reset
  Demultiplexer demultiplexer_1 (.out0(out_2), .out1(out_3), .in(1'b1), .sel(d_ff_2_q));  // open: en
endmodule
